# Fritzing sketch GIP (saved by Fritzing 0.8.7b)
breadboards: 1

parts:
  Mod1 = Raspberry Pi Pico
  U1 = L9110 H-bridge module [part_number="L9110 H-bridge"]
  J2 = Power Jack [package=power_jack_combo]
  R1 = Resistor [tolerance=±5% resistance=270 package=THT]
  R2 = Resistor [tolerance=±5% resistance=47 package=THT]
  BAT1 = Battery Holders [package=lipo-1100mAh]
  J3 = Basic Servo
  Part3 = Adafruit PowerBoost 1000C [part_number="Adafruit #2465"]
  S1 = SWITCH_SPDT [package=kps-1290]
  U2 = RELAY [package=relay-jzc]
  M2 = DC Motor
  A1 = Raspberry Pi Pico W

nets:
  N1: Mod1.pin_1, A1.pin_2
  N2: Mod1.pin_2, A1.pin_1
  GND: Mod1.pin_3, Mod1.pin_8, Mod1.pin_13, Mod1.pin_18, Mod1.pin_23, Mod1.pin_28, Mod1.pin_33, Mod1.pin_38, Mod1.pin_42, U1.GND, J2.GND, R1.Pin_0, BAT1.-, J3.gnd, Part3.GND, U2.MAIN, U2.COIL1, A1.pin_3, A1.pin_8, A1.pin_13, A1.pin_18, A1.pin_23, A1.pin_28, A1.pin_33, A1.pin_38, A1.pin_42
  N3: Mod1.pin_29, J3.pulse
  N4: Mod1.pin_31, U1.A-IB
  N5: Mod1.pin_32, U1.A-IA
  N6: Mod1.pin_39, J3.vcc, Part3.5.0V, A1.pin_39
  N7: U1.VCC, R1.Pin_1, R2.Pin_1
  N8: U1.MOTOR_A-A, M2.pin_2
  N9: U1.MOTOR_A-B, M2.pin_1
  N10: J2.PWR, Part3.VBUS, U2.COIL2
  N11: BAT1.+, Part3.VLIPO
  N12: Part3.ENABLE, S1.P
  N13: S1.S, U2.NC

notes:
  1350mAh 3.7V

custom parts:
  Raspberry Pi Pico: Raspberry Pi Pico. Based around the RP2040 microcontroller the Pico is a low cost microcontroller device bringing Raspberry Pi quality, cost, and easy of use to the microcontroller space. Jan 2021, Split part in to two versions: tht (this one) and SMD. This one will drill holes for a .1 in header in pcb to allow plugging in the module as well as providing pads to solder the module to the top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
  Adafruit PowerBoost 1000C: PowerBoost 1000C is the perfect power supply for your portable project! With a built-in load-sharing battery charger circuit, you'll be able to keep your power-hungry project running even while recharging the battery! This little DC/DC boost converter module can be powered by any 3.7V LiIon/LiPoly battery, and convert the battery output to 5.2V DC for running your 5V projects.
  Raspberry Pi Pico W: Raspberry Pi Pico W. Based around the RP2040 microcontroller the Pico W is a low cost microcontroller device bringing Raspberry Pi quality, cost, and easy of use to the microcontroller space. The areas marked KEEPOUT in pcb silkscreen should not have traces running through them to avoid shorts on a soldered in module!
