# Fritzing sketch GIP_final_noPowerBoost (saved by Fritzing 0.8.7b)

parts:
  Mod1 = Raspberry Pi Pico
  U1 = L9110 H-bridge module [part_number="L9110 H-bridge"]
  J2 = Power Jack [package=power_jack_combo]
  J3 = Basic Servo
  S1 = SWITCH_SPDT [package=kps-1290]
  M2 = DC Motor
  D1 = SOLAR-IXYS [package=solarbit-12x1]
  Part4 = USB LiPoly Charger
  D3 = Diode [package=diode-1n4001]
  D4 = Diode [package=diode-1n4001]
  A2 = Raspberry Pi Pico W
  D5 = Diode [package=diode-1n4001]

nets:
  N1: Mod1.pin_1, A2.pin_2
  N2: Mod1.pin_2, A2.pin_1
  N3: Mod1.pin_29, J3.pulse
  N4: Mod1.pin_31, U1.A-IB
  N5: Mod1.pin_32, U1.A-IA
  GND: Mod1.pin_38, Mod1.pin_42, U1.GND, J3.gnd, S1.S
  VCC: Mod1.pin_39, U1.VCC, J3.vcc, Part4.VBAT, D3.A, D4.A, A2.pin_39
  N6: U1.MOTOR_A-A, M2.pin_2
  N7: U1.MOTOR_A-B, M2.pin_1
  GND_2: J2.GND, S1.P, D1.C, Part4.GND, A2.pin_3, A2.pin_8, A2.pin_13, A2.pin_23, A2.pin_33, A2.pin_38, A2.pin_42, D5.A, D5.C
  N8: J2.PWR, D4.C, A2.pin_25
  N9: D1.A, D3.C

notes:
  Powerbank

custom parts:
  Raspberry Pi Pico: Raspberry Pi Pico. Based around the RP2040 microcontroller the Pico is a low cost microcontroller device bringing Raspberry Pi quality, cost, and easy of use to the microcontroller space. Jan 2021, Split part in to two versions: tht (this one) and SMD. This one will drill holes for a .1 in header in pcb to allow plugging in the module as well as providing pads to solder the module to the top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
  Raspberry Pi Pico W: Raspberry Pi Pico W. Based around the RP2040 microcontroller the Pico W is a low cost microcontroller device bringing Raspberry Pi quality, cost, and easy of use to the microcontroller space. The areas marked KEEPOUT in pcb silkscreen should not have traces running through them to avoid shorts on a soldered in module!
